# Fritzing sketch magspoof (saved by Fritzing 0.9.5d)
breadboards: 1

parts:
  Part1 = Arduino Pro Mini (5V)
  IC1 = L293D [package=THT]
  L1 = Inductor [package="400 mil [THT]"]
  S1 = Pushbutton [package="[THT]"]

nets:
  VCC: Part1.VCC, IC1.+Vmotor, IC1.+V
  GND: Part1.GND, IC1.0V, S1.Pin_2
  PIN_BUTTON: Part1.D9, S1.Pin_4
  PIN_B: Part1.D8, IC1.In_2
  PIN_A: Part1.D7, IC1.In_1
  PIN_ENABLE: Part1.D6, IC1.Enable_1
  COIL_A: IC1.Out_1_(_Controlled_by_Enable_1_), L1.pin_0
  COIL_B: IC1.Out_2_(_Controlled_by_Enable_1_), L1.pin_1
